// Logisim project ALU.circ as structural Verilog: 1 circuit, main circuit one_bit_alu
// 1-bit ALU
module one_bit_alu (
  input  A,
  input  B,
  input  Cin,
  input  AluOp,
  output AluOut,
  output Cout
);

  wire adder_1_out, nand_1_out;

  Adder #(.width(1)) adder_1 (.a(A), .b(B), .out(adder_1_out), .cin(Cin), .cout(Cout));
  nand nand_1 (nand_1_out, A, B);
  Multiplexer multiplexer_1 (.in0(adder_1_out), .in1(nand_1_out), .out(AluOut), .sel(AluOp));
endmodule
